# Fritzing sketch IC_4017B_Graph_PushDetect (saved by Fritzing 0.8.3b)
breadboards: 2

parts:
  Bauteil1 = Arduino Uno (Rev3)
  D1 = LED_BARGRAPH_10 [package=led_bargaph_10]
  R1 = Resistor [tolerance=±5% resistance=220 package=THT]
  LED1 = LED - 5mm [color="Red (633nm)" package="5 mm [THT]"]
  S1 = Pushbutton [package="[THT]"]
  R2 = Resistor [tolerance=±5% resistance=300 package=THT]
  Decade_Counter_4017 = IC, DIP package, 16 pins [chip_label=IC]

nets:
  N1: Bauteil1.GND, D1.J_C, D1.I_C, D1.H_C, D1.G_C, D1.F_C, D1.E_C, D1.D_C, D1.C_C, D1.B_C, D1.A_C, LED1.cathode, R2.Pin_1, Decade_Counter_4017.pin8, Decade_Counter_4017.pin13
  N2: Bauteil1.D8, S1.Pin_1, S1.Pin_2, R2.Pin_0
  N3: Bauteil1.D2, Decade_Counter_4017.pin14
  N4: Bauteil1.D3_PWM, Decade_Counter_4017.pin15
  N5: Bauteil1.5V, S1.Pin_3, S1.Pin_4, Decade_Counter_4017.pin16
  N6: D1.A_A, Decade_Counter_4017.pin3
  N7: D1.B_A, Decade_Counter_4017.pin2
  N8: D1.C_A, Decade_Counter_4017.pin4
  N9: D1.D_A, Decade_Counter_4017.pin7
  N10: D1.E_A, Decade_Counter_4017.pin10
  N11: D1.F_A, Decade_Counter_4017.pin1
  N12: D1.G_A, Decade_Counter_4017.pin5
  N13: D1.H_A, Decade_Counter_4017.pin6
  N14: D1.I_A, Decade_Counter_4017.pin9
  N15: D1.J_A, Decade_Counter_4017.pin11
  N16: R1.Pin_0, LED1.anode

notes:
  /*
  * Simple LED Bar graph control using a 4017 counter and a pushbutton
  * The 4017 is used to save pins on the arduino.
  * written by Fabian Moro´n Zirfas
  * based on work by Leonel Machava
  * http://codentronix.com
  * http://codentronix.com/2011/06/05/arduino-led-bar-graph-driven-by-a-4017-counter/
  * This code is release under the "MIT License" available at
  * http://www.opensource.org/licenses/mit-license.php
  *
  * and the Arduino Button Example
  * http://arduino.cc/en/Tutorial/Button
  * created 2005
  * by DojoDave <http://www.0j0.org>
  * modified 30 Aug 2011
  * by Tom Igoe
  *
  * CD4017B Datasheet
  * http://www.ti.com/lit/ds/symlink/cd4017b.pdf
  *
  * Pin Functions CD4017B
  *
  * PIN 16 - V DC
  * PIN 15 - RESET
  * PIN 14 - CLOCK
  * PIN 13 - CLOCK INHIBIT (STOP COUNTING) not used need to be GND
  * PIN 12 - CARRY OUT (INDICATE DECIMAL) not used need to be GND
  * PIN 11 - 9
  * PIN 10 - 4
  * PIN 09 - 8
  * PIN 08 - GND
  * PIN 07 - 3
  * PIN 06 - 7
  * PIN 05 - 6
  * PIN 04 - 2
  * PIN 03 - 0
  * PIN 02 - 1
  * PIN 01 - 5
  */
  int clockPin = 2; // this pulses the clock
  int buttonPin = 8; // this is for the pushbutton
  int buttonState = 0;// variable for reading the pushbutton status
  void setup() {
  pinMode(clockPin,OUTPUT);
  pinMode(buttonPin, INPUT);
  }
  void loop() {
  /**
  * Read the state of the button
  */
  buttonState = digitalRead(buttonPin);
  // check if the pushbutton is pressed.
  // if it is, the buttonState is HIGH:
  if (buttonState == HIGH) {
  digitalWrite(clockPin,LOW);
  }
  else {
  // button is pressed
  digitalWrite(clockPin,HIGH);
  }
  }
