# Fritzing sketch l293d (saved by Fritzing 0.9.0b)
breadboards: 2

parts:
  IC1 = L293D [package=THT]
  M2 = DC Motor
  VCC1 = Battery block 9V
  M1 = DC Motor
  Bauteil1 = Arduino Uno (Rev3)
  part = DC Motor  # not connected

nets:
  N1: IC1.Enable_1, Bauteil1.D3_PWM
  N2: IC1.In_1, Bauteil1.D6_PWM
  N3: IC1.Out_1_(_Controlled_by_Enable_1_), M2.pin_2
  N4: IC1.0V, VCC1.-, Bauteil1.GND
  N5: IC1.Out_2_(_Controlled_by_Enable_1_), M2.pin_1
  N6: IC1.In_2, Bauteil1.D5_PWM
  N7: IC1.+Vmotor, VCC1.+, Bauteil1.VIN
  N8: IC1.Enable_2, Bauteil1.D9_PWM
  N9: IC1.In_3, Bauteil1.D11_PWM/MOSI
  N10: IC1.Out_3_(_Controlled_by_Enable_2_), M1.pin_2
  N11: IC1.Out_4_(_Controlled_by_Enable_2_), M1.pin_1
  N12: IC1.In_4, Bauteil1.D10_PWM/SS
  N13: IC1.+V, Bauteil1.5V
