# Fritzing sketch pi-l293d (saved by Fritzing 0.9.2b)
breadboards: 2

parts:
  Raspberry_Pi1 = Raspberry Pi 2  # not connected
  J1 = T Cobbler Plus
  IC1 = L293D [package=THT]
  M1 = DC Motor
  VCC1 = 4 x AAA Battery Mount

nets:
  N1: J1.5.0V#3, IC1.In_1
  N2: J1.GND#5, IC1.In_2
  N3: J1.MISO, IC1.+V
  N4: J1.CE1, IC1.Enable_1
  N5: IC1.Out_1_(_Controlled_by_Enable_1_), M1.pin_2
  N6: IC1.0V, VCC1.-
  N7: IC1.Out_2_(_Controlled_by_Enable_1_), M1.pin_1
  N8: IC1.+Vmotor, VCC1.+

custom parts:
  T Cobbler Plus: The T-Cobbler Plus is an add on prototyping board from Adafruit specifically designed for the Raspberry Pi B+ that can break out all those tasty power, GPIO, I2C and SPI pins from the 40-pin header onto a solderless breadboard. This set will make "cobbling together" prototypes with the Pi super easy. The T-Cobbler Plus can plug into any solderless breadboard.
