# Fritzing sketch SevenSegmentDisplay (saved by Fritzing 0.8.3b)
breadboards: 2

parts:
  Bauteil1 = Arduino Uno (Rev3)
  U1 = 7-SEGMENT-DISPLAY [package=7-segment-display]
  R1 = Resistor [tolerance=±5% resistance=330 package=THT]
  R2 = Resistor [tolerance=±5% resistance=330 package=THT]
  R3 = Resistor [tolerance=±5% resistance=330 package=THT]
  R4 = Resistor [tolerance=±5% resistance=330 package=THT]
  R5 = Resistor [tolerance=±5% resistance=330 package=THT]
  R6 = Resistor [tolerance=±5% resistance=330 package=THT]
  R7 = Resistor [tolerance=±5% resistance=330 package=THT]
  R8 = Resistor [tolerance=±5% resistance=330 package=THT]

nets:
  N1: Bauteil1.GND, U1.C, U1.F
  N2: Bauteil1.D9_PWM, R6.Pin_0
  N3: Bauteil1.D10_PWM/SS, R5.Pin_0
  N4: Bauteil1.D1/TX, R1.Pin_0
  N5: Bauteil1.D2, R2.Pin_0
  N6: Bauteil1.D4, R3.Pin_0
  N7: Bauteil1.D5_PWM, R4.Pin_0
  N8: Bauteil1.D6_PWM, R8.Pin_0
  N9: Bauteil1.D7, R7.Pin_0
  N10: U1.E, R5.Pin_1
  N11: U1.D, R1.Pin_1
  N12: U1.G1, R2.Pin_1
  N13: U1.DP, R3.Pin_1
  N14: U1.B, R4.Pin_1
  N15: U1.A, R8.Pin_1
  N16: U1.G2, R7.Pin_1
  N17: U1.G, R6.Pin_1

notes:
  use Soda lib https://github.com/fabiantheblind/Soda
