# Fritzing sketch blink-different-pin (saved by Fritzing 0.8.7b)
breadboards: 1

parts:
  Bauteil1 = Arduino Uno (Rev3)
  LED1 = LED - 5mm [color="Red (633nm)" package="5 mm [THT]"]
  R1 = Resistor [tolerance=±5% resistance=220 package=THT]

nets:
  N1: Bauteil1.D12/MISO, R1.Pin_1
  N2: Bauteil1.GND, LED1.cathode
  N3: LED1.anode, R1.Pin_0
