# Fritzing sketch blink (saved by Fritzing 0.8.5b)
breadboards: 1

parts:
  LED1 = LED - 5mm [color="Red (633nm)" package="5 mm [THT]"]
  Bauteil1 = Arduino Uno (Rev3)

nets:
  N1: LED1.cathode, Bauteil1.GND
  N2: LED1.anode, Bauteil1.D13/SCK
