# Fritzing sketch pi-blink (saved by Fritzing 0.9.1b)
breadboards: 1

parts:
  Raspberry_Pi_B_rev1 = Raspberry Pi B rev1
  R1 = Resistor [tolerance=±5% resistance=220 package=THT]
  LED1 = smd LED [color="Red (633nm)" package="0805 [SMD]"]

nets:
  N1: Raspberry_Pi_B_rev1.GND, LED1.cathode
  N2: Raspberry_Pi_B_rev1.GPIO_21, R1.Pin_0
  N3: R1.Pin_1, LED1.anode
