# Fritzing sketch button_pull_up (saved by Fritzing 0.9.1b)
breadboards: 1

parts:
  Part1 = Arduino Uno (Rev3)
  S1 = Pushbutton [package=THT]

nets:
  N1: Part1.GND, S1.leg0
  N2: Part1.D2, S1.leg1
