# Fritzing sketch pi-button_pull_up (saved by Fritzing 0.9.1b)
breadboards: 1

parts:
  Raspberry_Pi_B_rev1 = Raspberry Pi B rev1
  S1 = Pushbutton [package="[THT]"]

nets:
  N1: Raspberry_Pi_B_rev1.GPIO_21, S1.Pin_1, S1.Pin_2
  N2: Raspberry_Pi_B_rev1.GND, S1.Pin_3, S1.Pin_4
