# Fritzing sketch capacitive_touch_paperclip (saved by Fritzing 0.9.0b)
breadboards: 1

parts:
  Part1 = Arduino Uno (Rev3)
  R1 = Resistor [tolerance=±5% resistance=1M package=THT]
  LED1 = LED - 5mm [color="Red (633nm)" package="5 mm [THT]"]
  R2 = Resistor [tolerance=±5% resistance=220 package=THT]

nets:
  N1: Part1.D12/MISO, R2.Pin_1
  N2: Part1.GND, LED1.cathode
  N3: Part1.D2, R1.Pin_1
  N4: Part1.5V, R1.Pin_0
  N5: LED1.anode, R2.Pin_0

notes:
  Use some cunductive material at the end of this wire. Cupper foil, a paper clip something else
