# Fritzing sketch pi-infrared (saved by Fritzing 0.9.2b)
breadboards: 1

parts:
  Raspberry_Pi1 = Raspberry Pi 2  # not connected
  J1 = T Cobbler Plus
  IR1 = TSOP312.., 314.. [package=THT]
  R1 = Resistor [tolerance=±5% resistance=1k package=THT]
  R2 = Resistor [tolerance=±5% resistance=150 package=THT]

nets:
  N1: J1.3V3, R2.Pin_1
  N2: J1.CE1, IR1.GND
  N3: J1.EED, IR1.Vs
  N4: IR1.Data, R1.Pin_0
  N5: R1.Pin_1, R2.Pin_0

notes:
  WARNING! The IR sensors we use have a different schematic then this one. (PPSEN 10266 https://www.sparkfun.com/datasheets/Sensors/Infrared/tsop382.pdf )
  Make sure you connect the
  - V to the 3,3V with the resistors
  - DATA to the pin you want to use
  - GND to ground
  The schematic in this fritzing setuo is wrong and just build visually

custom parts:
  T Cobbler Plus: The T-Cobbler Plus is an add on prototyping board from Adafruit specifically designed for the Raspberry Pi B+ that can break out all those tasty power, GPIO, I2C and SPI pins from the 40-pin header onto a solderless breadboard. This set will make "cobbling together" prototypes with the Pi super easy. The T-Cobbler Plus can plug into any solderless breadboard.
