# Fritzing sketch blink_mosfet (saved by Fritzing 0.9.9b)
breadboards: 1

parts:
  Part1 = Arduino Uno (Rev3)
  Q1 = Basic FET N-Channel [package="D2Pak [SMD]"]
  R1 = Resistor [tolerance=±5% power=0.25 resistance=680 package=THT]
  LED1 = LED - 5mm [color="Red (633nm)" current=0.030 package="5 mm [THT]"]
  VCC1 = Battery block 9V

nets:
  N1: Part1.D9_PWM, Q1.Gate
  N2: Part1.GND, LED1.cathode, VCC1.-
  N3: Q1.drain, R1.Pin_1
  N4: Q1.source, VCC1.+
  N5: R1.Pin_0, LED1.anode

notes:
  Make sure to look up the datasheet for your mosfet.
  S (Source) to power supply
  D (Drain) to consumer
  G (Gate) to MCU
