# Fritzing sketch optocoupler (saved by Fritzing 0.8.7b)
circuit board: 6.9215cm x 5.33756cm
breadboards: 1

parts:
  U1 = Optocoupler [package=THT]
  Arduino2 = Arduino Uno (Rev3)
  LED2 = LED - 5mm [color="Red (633nm)" package="5 mm [THT]"]
  R3 = Resistor [tolerance=±5% resistance=220 package=THT]
  VCC1 = 4 x AAA Battery Mount
  R2 = Resistor [tolerance=±5% resistance=220 package=THT]

nets:
  N1: U1.Pin_1, R2.Pin_1
  N2: U1.Pin_2, Arduino2.GND
  N3: U1.Pin_4, VCC1.-
  N4: U1.Pin_5, LED2.cathode
  N5: Arduino2.D11_PWM/MOSI, R2.Pin_0
  N6: LED2.anode, R3.Pin_0
  N7: R3.Pin_1, VCC1.+

notes:
  An optocoupler can be used to control a circuit that's completely isolated from your microcontroller in order to avoid the risk of short-circuit. In this case, imagine that the LED + battery pack combo is a hacked toy that you're turning on and off with the Arduino.
