# Fritzing sketch pushbutton (saved by Fritzing 0.8.7b)
breadboards: 1

parts:
  S1 = Pushbutton [package=THT]
  R1 = Resistor [tolerance=±5% resistance=10k package=THT]
  LED1 = LED - 5mm [color="Red (633nm)" package="5 mm [THT]"]
  R2 = Resistor [tolerance=±5% resistance=220 package=THT]
  Bauteil1 = Arduino Uno (Rev3)
  part = Arduino Uno (Rev3)  # not connected

nets:
  N1: S1.leg0, R1.Pin_0, Bauteil1.D2
  N2: S1.leg1, Bauteil1.5V
  N3: R1.Pin_1, LED1.cathode, Bauteil1.GND
  N4: LED1.anode, R2.Pin_0
  N5: R2.Pin_1, Bauteil1.D13/SCK
