# Fritzing sketch pi-relay-and-transistor (saved by Fritzing 0.9.1b)
breadboards: 1

parts:
  J1 = Cobbler Plus
  Q1 = PNP-Transistor [package="TO92 [THT]"]
  K1 = Relay [part_number=FRS1B-S package=THT]
  VCC1 = 4 x AAA Battery Mount
  LED1 = smd LED [color="Red (633nm)" package="1206 [SMD]"]
  R1 = Resistor [tolerance=±5% resistance=220 package=THT]

nets:
  N1: J1.3V3, Q1.C
  N2: J1.EEC, Q1.B
  N3: J1.GND#29, K1.COIL1
  N4: Q1.E, K1.COIL2
  N5: K1.C1, K1.C2, LED1.cathode
  N6: K1.B, VCC1.-
  N7: VCC1.+, R1.Pin_1
  N8: LED1.anode, R1.Pin_0

custom parts:
  Cobbler Plus: The Cobbler Plus is an add on prototyping board from Adafruit specifically designed for the Raspberry Pi B+ that can break out all those tasty power, GPIO, I2C and SPI pins from the 40-pin header onto a solderless breadboard. This set will make "cobbling together" prototypes with the Pi super easy. The Cobbler Plus can plug into any solderless breadboard.
