# Fritzing sketch pi-relay (saved by Fritzing 0.9.2b)
breadboards: 1

parts:
  Raspberry_Pi_B_rev1 = Raspberry Pi B rev1
  K1 = Relay [part_number=FRS1B-S package=THT]
  VCC1 = 4 x AAA Battery Mount
  R1 = Resistor [tolerance=±5% resistance=220 package=THT]
  LED1 = LED - 5mm [color="Red (633nm)" package="5 mm [THT]"]

nets:
  N1: Raspberry_Pi_B_rev1.GPIO_21, K1.COIL1
  N2: Raspberry_Pi_B_rev1.GND, K1.COIL2
  N3: K1.A, VCC1.+
  N4: K1.C1, K1.C2, R1.Pin_0
  N5: VCC1.-, LED1.cathode
  N6: R1.Pin_1, LED1.anode
