# Fritzing sketch relay (saved by Fritzing 0.8.7b)
breadboards: 1

parts:
  Arduino_Uno = Arduino Uno (Rev3)
  R1 = Resistor [tolerance=±5% resistance=220 package=THT]
  LED1 = LED - 5mm [color="Red (633nm)" package="5 mm [THT]"]
  part = 4 x AAA Battery Mount  # not connected
  VCC1 = 4 x AAA Battery Mount
  U1 = RELAY-2 [package=relay-g5v]

nets:
  N1: Arduino_Uno.D13/SCK, U1.9
  N2: Arduino_Uno.GND, U1.2
  N3: R1.Pin_0, LED1.anode
  N4: R1.Pin_1, VCC1.+
  N5: LED1.cathode, U1.5
  N6: VCC1.-, U1.10
