# Fritzing sketch tiltswitch (saved by Fritzing 0.8.7b)
breadboards: 1

parts:
  LED1 = LED - 5mm [color="Red (633nm)" package="5 mm [THT]"]
  S1 = Tilt Switch [package=THT]
  R1 = Resistor [tolerance=±5% resistance=100k package=THT]
  Bauteil1 = Arduino Uno (Rev3)
  R2 = Resistor [tolerance=±5% resistance=220 package=THT]

nets:
  N1: LED1.cathode, S1.Pin_2, Bauteil1.GND
  N2: LED1.anode, R2.Pin_0
  N3: S1.Pin_1, R1.Pin_1, Bauteil1.D2
  N4: R1.Pin_0, Bauteil1.5V
  N5: Bauteil1.D12/MISO, R2.Pin_1
