# Fritzing sketch pi-tiltswitch (saved by Fritzing 0.9.1b)
breadboards: 1

parts:
  Raspberry_Pi_B_rev1 = Raspberry Pi B rev1
  S2 = Tilt Switch [package=THT]

nets:
  N1: Raspberry_Pi_B_rev1.GPIO_21, S2.Pin_1
  N2: Raspberry_Pi_B_rev1.GND, S2.Pin_2
