# Fritzing sketch tiltswitch (saved by Fritzing 0.8.3b)
breadboards: 1

parts:
  Bauteil1 = Arduino Uno (Rev3)
  LED1 = LED - 5mm [color="Red (633nm)" package="5 mm [THT]"]
  S1 = Tilt Switch [package=THT]
  R1 = Resistor [tolerance=±5% resistance=100k package=THT]

nets:
  N1: Bauteil1.GND, LED1.cathode, S1.Pin_2
  N2: Bauteil1.D13/SCK, LED1.anode
  N3: Bauteil1.D2, S1.Pin_1, R1.Pin_1
  N4: Bauteil1.5V, R1.Pin_0

notes:
  /**
  * Simple tilt switch (pin 2) sketch.
  * Turns a LED on pin 13 on and off
  *
  */
  int ledpin = 13; // for output
  int tiltpin = 2; // tiltswitch in put
  int is_on = 0;// boolean
  void setup(){
  pinMode(ledpin, OUTPUT); // init
  pinMode(tiltpin, INPUT); // inti
  }
  void loop(){
  is_on = digitalRead(tiltpin); // read from the switch
  if(is_on){
  digitalWrite(ledpin,HIGH); // on
  }else{
  digitalWrite(ledpin,LOW); // off
  }
  }
