# Fritzing sketch transistor (saved by Fritzing 0.9.0b)
breadboards: 1

parts:
  Q1 = NPN-Transistor [package="TO92 [THT]"]
  LED1 = LED - 5mm [color="Red (633nm)" package="5 mm [THT]"]
  R1 = Resistor [tolerance=±5% resistance=220 package=THT]
  Bauteil1 = Arduino Uno (Rev3)
  part = Arduino Uno (Rev3)  # not connected

nets:
  N1: Q1.E, Bauteil1.5V
  N2: Q1.B, Bauteil1.D13/SCK
  N3: Q1.C, R1.Pin_1
  N4: LED1.cathode, Bauteil1.GND
  N5: LED1.anode, R1.Pin_0
