# Fritzing sketch pi-transistor (saved by Fritzing 0.9.2b)
breadboards: 1

parts:
  Raspberry_Pi_B_rev1 = Raspberry Pi B rev1
  Q1 = NPN-Transistor [package="TO92 [THT]"]
  R1 = Resistor [tolerance=±5% resistance=220 package=THT]
  LED1 = LED - 5mm [color="Red (633nm)" package="5 mm [THT]"]

nets:
  N1: Raspberry_Pi_B_rev1.3V3, Q1.E
  N2: Raspberry_Pi_B_rev1.GND, LED1.cathode
  N3: Raspberry_Pi_B_rev1.GPIO_21, Q1.B
  N4: Q1.C, R1.Pin_1
  N5: R1.Pin_0, LED1.anode
