# Fritzing sketch transistor (saved by Fritzing 0.8.5b)
breadboards: 1

parts:
  Bauteil1 = Arduino Uno (Rev3)
  Q1 = NPN-Transistor [package="TO92 [THT]"]
  LED1 = LED - 5mm [color="Red (633nm)" package="5 mm [THT]"]
  R1 = Resistor [tolerance=±5% resistance=220 package=THT]

nets:
  N1: Bauteil1.D13/SCK, Q1.B
  N2: Bauteil1.5V, Q1.E
  N3: Bauteil1.GND, LED1.cathode
  N4: LED1.anode, R1.Pin_0
